# Fritzing sketch 2x7-segment (saved by Fritzing 0.9.0b)
breadboards: 1

parts:
  U2 = 7-SEGMENT-DISPLAY [package=7-segment-display]
  U3 = 7-SEGMENT-DISPLAY [package=7-segment-display]
  Part1 = Arduino Uno (Rev3)

nets:
  N1: U2.E, U3.E, Part1.D5_PWM
  N2: U2.D, U3.D, Part1.D4
  N3: U2.G1, U3.G1, Part1.D3_PWM
  N4: U2.DP, U3.DP, Part1.D2
  N5: U2.A, U3.A, Part1.D8
  N6: U2.G2, U3.G2, Part1.D7
  N7: U2.F, Part1.D11_PWM/MOSI
  N8: U2.G, U3.G, Part1.D6_PWM
  N9: U3.F, Part1.D12/MISO
