# Fritzing sketch 7-segment (saved by Fritzing 0.9.0b)
breadboards: 1

parts:
  U2 = 7-SEGMENT-DISPLAY [package=7-segment-display]
  Part1 = Arduino Uno (Rev3)
  R1 = Resistor [tolerance=±5% resistance=220 package=THT]
  R2 = Resistor [tolerance=±5% resistance=220 package=THT]
  R3 = Resistor [tolerance=±5% resistance=220 package=THT]
  R4 = Resistor [tolerance=±5% resistance=220 package=THT]
  R5 = Resistor [tolerance=±5% resistance=220 package=THT]
  R6 = Resistor [tolerance=±5% resistance=220 package=THT]
  R7 = Resistor [tolerance=±5% resistance=220 package=THT]

nets:
  N1: U2.E, R3.Pin_1
  N2: U2.D, R4.Pin_0
  N3: U2.G1, R2.Pin_0
  N4: U2.C, Part1.GND
  N5: U2.DP, R1.Pin_0
  N6: U2.A, R6.Pin_1
  N7: U2.G2, R5.Pin_1
  N8: U2.G, R7.Pin_1
  N9: Part1.D8, R6.Pin_0
  N10: Part1.D2, R1.Pin_1
  N11: Part1.D3_PWM, R2.Pin_1
  N12: Part1.D4, R4.Pin_1
  N13: Part1.D5_PWM, R3.Pin_0
  N14: Part1.D6_PWM, R7.Pin_0
  N15: Part1.D7, R5.Pin_0
